# Fritzing sketch 3_pin_ryg_example (saved by Fritzing 0.9.3b)
breadboards: 1

parts:
  Part1 = Arduino Uno (Rev3)
  LED1 = LED - 5mm [color="Red (633nm)" package="5 mm [THT]"]
  LED3 = LED - 5mm [color="Orange (612nm)" package="5 mm [THT]"]
  LED4 = LED - 5mm [color="Green (555nm)" package="5 mm [THT]"]
  R1 = Resistor [tolerance=±5% resistance=470 package=THT]
  S1 = Pushbutton [package="[THT]"]
  LED5 = LED - 5mm [color="Red (633nm)" package="5 mm [THT]"]
  LED6 = LED - 5mm [color="Orange (612nm)" package="5 mm [THT]"]
  LED7 = LED - 5mm [color="Green (555nm)" package="5 mm [THT]"]
  R2 = Resistor [tolerance=±5% resistance=470 package=THT]
  S2 = Pushbutton [package="[THT]"]
  S3 = Pushbutton [package="[THT]"]

nets:
  N1: Part1.D8, LED7.anode
  N2: Part1.D9_PWM, Part1.D1/TX, R1.Pin_1, S1.Pin_1, S1.Pin_2, S1.Pin_3, S1.Pin_4, R2.Pin_1, S2.Pin_1, S2.Pin_2, S2.Pin_3, S2.Pin_4, S3.Pin_1, S3.Pin_2, S3.Pin_3, S3.Pin_4
  N3: Part1.D6_PWM, LED5.anode
  N4: Part1.D7, LED6.anode
  N5: LED1.cathode, LED3.cathode, LED4.cathode, R1.Pin_0
  N6: LED5.cathode, LED6.cathode, LED7.cathode, R2.Pin_0

notes:
  head_1
  sensor_1
  head_2
  sensor_3
  470k
  sensor_2
